// Logisim project Forwarding.circ as structural Verilog: 1 circuit, main circuit main
module main (
  input  [4:0] Ra,
  input  [4:0] Ex_Rd,
  input  [4:0] Mem_Rd,
  input  [4:0] Wb_Rd,
  output Ex,
  output Mem,
  output Wb
);

  wire and_3_out, and_5_out, nand_1_out, nor_1_out, nor_2_out, nor_3_out, xor_4_out, xor_5_out;
  wire [4:0] xor_1_out, xor_2_out, xor_3_out;

  nand nand_1 (nand_1_out, ~Ra[0], ~Ra[1], ~Ra[2], ~Ra[3], ~Ra[4]);  // NAND_Gate
  assign xor_1_out = Ra ^ Ex_Rd;  // XOR_Gate xor_1, 5 bits wide
  assign xor_2_out = Ra ^ Mem_Rd;  // XOR_Gate xor_2, 5 bits wide
  assign xor_3_out = Ra ^ Wb_Rd;  // XOR_Gate xor_3, 5 bits wide
  nor nor_1 (nor_1_out, xor_1_out[0], xor_1_out[1], xor_1_out[2], xor_1_out[3], xor_1_out[4]);
  nor nor_2 (nor_2_out, xor_2_out[0], xor_2_out[1], xor_2_out[2], xor_2_out[3], xor_2_out[4]);
  nor nor_3 (nor_3_out, xor_3_out[0], xor_3_out[1], xor_3_out[2], xor_3_out[3], xor_3_out[4]);
  xor xor_4 (xor_4_out, nor_1_out, nor_2_out);
  ExactlyOne xor_5 (.out(xor_5_out), .in0(nor_1_out), .in1(nor_2_out), .in2(nor_3_out));
  and and_1 (Ex, nand_1_out, nor_1_out);
  and and_2 (Mem, nand_1_out, and_3_out);
  and and_3 (and_3_out, xor_4_out, nor_2_out);
  and and_4 (Wb, nand_1_out, and_5_out);
  and and_5 (and_5_out, xor_5_out, nor_3_out);
endmodule
