// Logisim project Processor.circ as structural Verilog: 11 circuits, main circuit MIPS32
module MIPS32 (
);

  wire and_1_out, Clock_out, comparator_1_lt, comparator_2_lt, compare_0_1_out_2, hazard_detector_1_ex,
       hazard_detector_1_mem, hazard_detector_2_ex, hazard_detector_2_mem, lui_selector_1_out_2,
       move_selector_1_m, multiplexer_10_out, multiplexer_11_out, multiplexer_16_out, multiplexer_17_out,
       not_1_out, not_2_out, registerfile_1_p3, slt_selector_1_muxer, table_b_selector_1_out, WE_2_q, WE_q;
  wire [1:0] func_q_2;
  wire [3:0] func_q, function_selector_1_out_2, mips_alu_1_p3, multiplexer_7_out, shift_left_1_1_out_2,
       shift_left_1_2_out_2;
  wire [4:0] multiplexer_1_out, multiplexer_4_out, multiplexer_8_out, Ra_q, Rb_q, registerfile_1_p4, Rw_2_q,
       Rw_q, shamt_q;
  wire [5:0] multiplexer_12_out, Op_q;
  wire [15:0] Imm_q;
  wire [26:0] multiplexer_4_out_2;
  wire [31:0] A_q, B_2_q, B_q, bit_extender_1_out, bit_extender_2_out, IF_ID_q, mips_alu_1_p5,
       mipsprogramrom_1_p2, multiplexer_2_out, multiplexer_3_out, multiplexer_5_out, multiplexer_6_out,
       multiplexer_13_out, multiplexer_14_out, multiplexer_15_out, pc_4_1_new, PC_q, registerfile_1_p1,
       registerfile_1_p7, registerfile_1_p8, shift_left_16_1_out_2;

  Register #(.width(32)) PC (.D(pc_4_1_new), .Q(PC_q), .clk(Clock_out));  // open: en, clr
  Clock Clock (.out(Clock_out));
  PC_4 pc_4_1 (.Old(PC_q), .New(pc_4_1_new));
  // MIPSProgramROM mipsprogramrom_1: pin names not known; wires that end beside it: PC_q, mipsprogramrom_1_p2
  Register #(.width(32)) IF_ID (.D(mipsprogramrom_1_p2), .Q(IF_ID_q), .clk(Clock_out));  // open: en, clr
  // RegisterFile registerfile_1: pin names not known; wires that end beside it: registerfile_1_p1, Clock_out, registerfile_1_p3, registerfile_1_p4, IF_ID_q[25:21], IF_ID_q[20:16], registerfile_1_p7, registerfile_1_p8
  Register #(.width(32)) A (.D(registerfile_1_p7), .Q(A_q), .clk(Clock_out));  // open: en, clr
  Register #(.width(32)) B (.D(registerfile_1_p8), .Q(B_q), .clk(Clock_out));  // open: en, clr
  Register #(.width(16)) Imm (.D(IF_ID_q[15:0]), .Q(Imm_q), .clk(Clock_out));  // open: en, clr
  Register #(.width(5)) Rw (.D(multiplexer_1_out), .Q(Rw_q), .clk(Clock_out));  // open: en, clr
  Multiplexer #(.width(5), .enable("false")) multiplexer_1 (
    .in0(IF_ID_q[15:11]), .in1(IF_ID_q[20:16]), .out(multiplexer_1_out), .sel(IF_ID_q[29]));
  Register #(.width(6)) Op (.D(IF_ID_q[31:26]), .Q(Op_q), .clk(Clock_out));  // open: en, clr
  Register #(.width(5)) shamt (.D(IF_ID_q[10:6]), .Q(shamt_q), .clk(Clock_out));  // open: en, clr
  Register #(.width(6)) func (.D(IF_ID_q[5:0]), .Q({func_q_2, func_q}), .clk(Clock_out));  // open: en, clr
  Register #(.width(5)) Ra (.D(IF_ID_q[25:21]), .Q(Ra_q), .clk(Clock_out));  // open: en, clr
  Register #(.width(5)) Rb (.D(IF_ID_q[20:16]), .Q(Rb_q), .clk(Clock_out));  // open: en, clr
  Register #(.width(1)) WE (.D(1'b1), .Q(WE_q), .clk(Clock_out));  // open: en, clr
  Hazard_Detector hazard_detector_1 (
    .Rd(Ra_q), .Mem_Rw(Rw_2_q), .Wb_Rw(registerfile_1_p4), .Ex(hazard_detector_1_ex),
    .Mem(hazard_detector_1_mem));
  Multiplexer #(.width(32), .enable("false")) multiplexer_2 (
    .in0(A_q), .in1(B_2_q), .out(multiplexer_2_out), .sel(hazard_detector_1_ex));
  Multiplexer #(.width(32), .enable("false")) multiplexer_3 (
    .in0(B_q), .in1(B_2_q), .out(multiplexer_3_out), .sel(hazard_detector_2_ex));
  Hazard_Detector hazard_detector_2 (
    .Rd(Rb_q), .Mem_Rw(Rw_2_q), .Wb_Rw(registerfile_1_p4), .Ex(hazard_detector_2_ex),
    .Mem(hazard_detector_2_mem));
  Multiplexer #(.width(32), .enable("false")) multiplexer_4 (
    .in0(multiplexer_2_out), .in1(registerfile_1_p1), .out({multiplexer_4_out_2, multiplexer_4_out}),
    .sel(hazard_detector_1_mem));
  Multiplexer #(.width(32), .enable("false")) multiplexer_5 (
    .in0(multiplexer_3_out), .in1(registerfile_1_p1), .out(multiplexer_5_out), .sel(hazard_detector_2_mem));
  assign bit_extender_1_out = {{16{Imm_q[15]}}, Imm_q};  // Bit_Extender bit_extender_1
  Shift_Left_1 shift_left_1_1 (.in_1(Op_q[3:0]), .out_2(shift_left_1_1_out_2));
  Function_Selector function_selector_1 (.in_1(func_q), .out_2(function_selector_1_out_2));
  Shift_Left_1 shift_left_1_2 (.in_1(func_q), .out_2(shift_left_1_2_out_2));
  Multiplexer #(.width(32), .enable("false")) multiplexer_6 (
    .in0(multiplexer_5_out), .in1(bit_extender_1_out), .out(multiplexer_6_out), .sel(Op_q[3]));
  Multiplexer #(.width(4), .enable("false")) multiplexer_7 (
    .in0(function_selector_1_out_2), .in1(shift_left_1_2_out_2), .out(multiplexer_7_out), .sel(func_q_2[1]));
  not not_1 (not_1_out, func_q[2]);
  Compare_0 compare_0_1 (.in_1(multiplexer_5_out), .out_2(compare_0_1_out_2));
  Multiplexer #(.width(5), .enable("false")) multiplexer_8 (
    .in0(multiplexer_4_out), .in1(shamt_q), .out(multiplexer_8_out), .sel(not_1_out));
  Shift_Left_16 shift_left_16_1 (.in_1(Imm_q), .out_2(shift_left_16_1_out_2));
  not not_2 (not_2_out, compare_0_1_out_2);
  Comparator #(.width(32)) comparator_1 (
    .a({multiplexer_4_out_2, multiplexer_4_out}), .b(multiplexer_6_out), .lt(comparator_1_lt));  // open: gt, eq
  Comparator #(.width(32), .mode("unsigned")) comparator_2 (
    .a({multiplexer_4_out_2, multiplexer_4_out}), .b(multiplexer_6_out), .lt(comparator_2_lt));  // open: gt, eq
  // Mips_ALU mips_alu_1: pin names not known; wires that end beside it: {multiplexer_4_out_2, multiplexer_4_out}, multiplexer_6_out, mips_alu_1_p3, multiplexer_8_out, mips_alu_1_p5
  Multiplexer #(.width(4), .enable("false")) multiplexer_9 (
    .in0(multiplexer_7_out), .in1(shift_left_1_1_out_2), .out(mips_alu_1_p3), .sel(Op_q[3]));
  Multiplexer #(.enable("false")) multiplexer_10 (
    .in0(compare_0_1_out_2), .in1(not_2_out), .out(multiplexer_10_out), .sel(func_q[0]));
  Multiplexer #(.enable("false")) multiplexer_11 (
    .in0(comparator_1_lt), .in1(comparator_2_lt), .out(multiplexer_11_out), .sel(multiplexer_12_out[0]));
  assign bit_extender_2_out = {{31{1'b0}}, multiplexer_11_out};  // Bit_Extender bit_extender_2
  SLT_Selector slt_selector_1 (.in_1(multiplexer_12_out[3:0]), .muxer(slt_selector_1_muxer));
  Multiplexer #(.width(6), .enable("false")) multiplexer_12 (
    .in0({func_q_2, func_q}), .in1(Op_q), .out(multiplexer_12_out), .sel(Op_q[3]));
  Multiplexer #(.width(32), .enable("false")) multiplexer_13 (
    .in0(mips_alu_1_p5), .in1(bit_extender_2_out), .out(multiplexer_13_out), .sel(slt_selector_1_muxer));
  Move_Selector move_selector_1 (.op3(Op_q[3]), .fun6(func_q_2[1]), .fun3(func_q[3]), .m(move_selector_1_m));
  Multiplexer #(.width(32), .enable("false")) multiplexer_14 (
    .in0(multiplexer_13_out), .in1({multiplexer_4_out_2, multiplexer_4_out}), .out(multiplexer_14_out),
    .sel(move_selector_1_m));
  LUI_Selector lui_selector_1 (.in_1(Op_q[3:0]), .out_2(lui_selector_1_out_2));
  Multiplexer #(.width(32), .enable("false")) multiplexer_15 (
    .in0(multiplexer_14_out), .in1(shift_left_16_1_out_2), .out(multiplexer_15_out),
    .sel(lui_selector_1_out_2));
  Multiplexer #(.enable("false")) multiplexer_16 (
    .in0(WE_q), .in1(multiplexer_10_out), .out(multiplexer_16_out), .sel(move_selector_1_m));
  Table_B_Selector table_b_selector_1 (.Last({func_q_2, func_q}), .First(Op_q), .out(table_b_selector_1_out));
  Multiplexer #(.enable("false")) multiplexer_17 (
    .in0(multiplexer_16_out), .in1(and_1_out), .out(multiplexer_17_out), .sel(table_b_selector_1_out));
  and and_1 (and_1_out, multiplexer_16_out, ~multiplexer_16_out);  // AND_Gate
  Register #(.width(32)) B_2 (.D(multiplexer_15_out), .Q(B_2_q), .clk(Clock_out));  // open: en, clr
  Register #(.width(5)) Rw_2 (.D(Rw_q), .Q(Rw_2_q), .clk(Clock_out));  // open: en, clr
  Register #(.width(1)) WE_2 (.D(multiplexer_17_out), .Q(WE_2_q), .clk(Clock_out));  // open: en, clr
  Register #(.width(32)) B_3 (.D(B_2_q), .Q(registerfile_1_p1), .clk(Clock_out));  // open: en, clr
  Register #(.width(5)) Rw_3 (.D(Rw_2_q), .Q(registerfile_1_p4), .clk(Clock_out));  // open: en, clr
  Register #(.width(1)) WE_3 (.D(WE_2_q), .Q(registerfile_1_p3), .clk(Clock_out));  // open: en, clr
endmodule

module PC_4 (
  input  [31:0] Old,
  output [31:0] New
);

  // Incrementer incrementer_1: pin names not known; wires that end beside it: Old[31:2], New[31:2]

  assign New[1:0] = Old[1:0];
endmodule

// SLL1
module Shift_Left_1 (
  input  [3:0] in_1,
  output [3:0] out_2
);

  wire not_1_out;

  and and_1 (out_2[0], in_1[3], not_1_out);
  not not_1 (not_1_out, in_1[3]);

  assign out_2[3:1] = in_1[2:0];
endmodule

// SL16
module Shift_Left_16 (
  input  [15:0] in_1,
  output [31:0] out_2
);

  wire [15:0] not_1_out;

  assign out_2[15:0] = in_1 & not_1_out;  // AND_Gate and_1, 16 bits wide
  assign not_1_out = ~in_1;  // NOT_Gate not_1, 16 bits wide

  assign out_2[31:16] = in_1;
endmodule

// Func Sel
module Function_Selector (
  input  [3:0] in_1,
  output [3:0] out_2
);

  or or_1 (out_2[0], in_1[0], in_1[3]);

  assign out_2[3:1] = {in_1[3], in_1[1], in_1[3]};
endmodule

// Eq 0
module Compare_0 (
  input  [31:0] in_1,
  output out_2
);

  wire [31:0] and_1_out, not_1_out, xnor_1_out;

  assign not_1_out = ~in_1;  // NOT_Gate not_1, 32 bits wide
  assign and_1_out = in_1 & not_1_out;  // AND_Gate and_1, 32 bits wide
  assign xnor_1_out = ~(and_1_out ^ in_1);  // XNOR_Gate xnor_1, 32 bits wide
  and and_2 (out_2, xnor_1_out[0], xnor_1_out[1], xnor_1_out[2], xnor_1_out[3], xnor_1_out[4], xnor_1_out[5], xnor_1_out[6], xnor_1_out[7], xnor_1_out[8], xnor_1_out[9], xnor_1_out[10], xnor_1_out[11], xnor_1_out[12], xnor_1_out[13], xnor_1_out[14], xnor_1_out[15], xnor_1_out[17], xnor_1_out[18], xnor_1_out[19], xnor_1_out[20], xnor_1_out[21], xnor_1_out[22], xnor_1_out[23], xnor_1_out[24], xnor_1_out[25], xnor_1_out[26], xnor_1_out[27], xnor_1_out[28], xnor_1_out[29], xnor_1_out[30], xnor_1_out[31], xnor_1_out[16]);
endmodule

// Mov Sel
module Move_Selector (
  input  op3,
  input  fun6,
  input  fun3,
  output m
);

  wire not_1_out, not_2_out;

  not not_1 (not_1_out, op3);
  not not_2 (not_2_out, fun6);
  and and_1 (m, not_1_out, not_2_out, fun3);
endmodule

// LUI Sel
module LUI_Selector (
  input  [3:0] in_1,
  output out_2
);

  wire [3:0] nand_1_out, not_1_out, xnor_1_out;

  assign nand_1_out = ~(in_1 & not_1_out);  // NAND_Gate nand_1, 4 bits wide
  assign not_1_out = ~in_1;  // NOT_Gate not_1, 4 bits wide
  assign xnor_1_out = ~(nand_1_out ^ in_1);  // XNOR_Gate xnor_1, 4 bits wide
  and and_1 (out_2, xnor_1_out[0], xnor_1_out[1], xnor_1_out[2], xnor_1_out[3]);
endmodule

// Hzd
module Hazard_Detector (
  input  [4:0] Rd,
  input  [4:0] Mem_Rw,
  input  [4:0] Wb_Rw,
  output Ex,
  output Mem
);

  wire and_3_out, nand_1_out, nor_1_out, nor_2_out, xor_3_out;
  wire [4:0] xor_1_out, xor_2_out;

  nand nand_1 (nand_1_out, ~Rd[0], ~Rd[1], ~Rd[2], ~Rd[3], ~Rd[4]);  // NAND_Gate
  assign xor_1_out = Rd ^ Mem_Rw;  // XOR_Gate xor_1, 5 bits wide
  assign xor_2_out = Rd ^ Wb_Rw;  // XOR_Gate xor_2, 5 bits wide
  nor nor_1 (nor_1_out, xor_1_out[0], xor_1_out[1], xor_1_out[2], xor_1_out[3], xor_1_out[4]);
  nor nor_2 (nor_2_out, xor_2_out[0], xor_2_out[1], xor_2_out[2], xor_2_out[3], xor_2_out[4]);
  xor xor_3 (xor_3_out, nor_1_out, nor_2_out);
  and and_1 (Ex, nand_1_out, nor_1_out);
  and and_2 (Mem, nand_1_out, and_3_out);
  and and_3 (and_3_out, xor_3_out, nor_2_out);
endmodule

// SLT Sel
module SLT_Selector (
  input  [3:0] in_1,
  output muxer
);

  wire not_1_out;

  not not_1 (not_1_out, in_1[2]);
  and and_1 (muxer, in_1[3], not_1_out, in_1[1]);
endmodule

// Tbl B Sel
module Table_B_Selector (
  input  [5:0] First,
  input  [5:0] Last,
  output out
);

  wire and_1_out, and_2_out, and_3_out, and_4_out, and_5_out, and_6_out, not_1_out, not_2_out, not_3_out,
       not_4_out, not_5_out, not_6_out, not_7_out, not_8_out, not_9_out, not_10_out, or_1_out;

  and and_1 (and_1_out, ~First[2], ~First[0], ~First[1], ~First[3], ~First[4], ~First[5]);  // AND_Gate
  not not_1 (not_1_out, First[4]);
  not not_2 (not_2_out, First[3]);
  not not_3 (not_3_out, First[4]);
  not not_4 (not_4_out, First[3]);
  not not_5 (not_5_out, First[4]);
  not not_6 (not_6_out, First[3]);
  not not_7 (not_7_out, Last[5]);
  not not_8 (not_8_out, Last[4]);
  not not_9 (not_9_out, Last[2]);
  not not_10 (not_10_out, Last[1]);
  and and_2 (and_2_out, not_1_out, not_2_out, First[0]);
  and and_3 (and_3_out, not_3_out, not_4_out, First[1]);
  and and_4 (and_4_out, not_5_out, not_6_out, First[2]);
  and and_5 (and_5_out, not_7_out, not_8_out, Last[3], not_9_out, not_10_out);
  or or_1 (or_1_out, and_2_out, and_3_out, and_4_out, First[5]);
  and and_6 (and_6_out, and_1_out, and_5_out);
  or or_2 (out, or_1_out, and_6_out);
endmodule
